// Logisim project 8_bit_cpu.circ as structural Verilog: 6 circuits, main circuit alu
module cpu (
  output [7:0] out_1,
  output [7:0] out_2,
  output [7:0] out_3,
  output [7:0] out_4
);

  wire alu_1_c, alu_1_z, button_1_out, C, clock_1_out, cu_1_ae, cu_1_alu_bus, cu_1_be, cu_1_c_e, cu_1_pc_inc,
       cu_1_pc_load, cu_1_ram_read, cu_1_ram_write, cu_1_z_e, d_ff_1_q, not_1_out, or_1_out, por_1_out,
       xnor_1_out, Z;
  wire [1:0] cu_1_asrc, cu_1_bsrc, cu_1_mem_counter;
  wire [2:0] cu_1_ctrl;
  wire [7:0] a_q, b_q, DBus_past_q, multiplexer_1_out, multiplexer_2_out, PC_q;

  Button button_1 (.out(button_1_out));
  Clock clock_1 (.out(clock_1_out));
  D_Flip_Flop d_ff_1 (.D(clock_1_out), .clk(or_1_out), .Q(d_ff_1_q));  // open: Qn, preset, reset
  or or_1 (or_1_out, por_1_out, button_1_out);
  POR #(.PorHighDuration(1)) por_1 (.out(por_1_out));
  Register DBus_past (.D(out_2), .en(1'b1), .Q(DBus_past_q), .clk(xnor_1_out), .clr(or_1_out));
  xnor xnor_1 (xnor_1_out, clock_1_out, d_ff_1_q);
  Register a (.D(out_1), .en(cu_1_ae), .clk(xnor_1_out), .Q(a_q), .clr(or_1_out));
  Register b (.D(out_1), .en(cu_1_be), .clk(xnor_1_out), .Q(b_q), .clr(or_1_out));
  cu cu_1 (
    .Clk(xnor_1_out), .R(or_1_out), .D_Bus(DBus_past_q), .Z(Z), .C(C), .Ctrl(cu_1_ctrl), .Asrc(cu_1_asrc),
    .Bsrc(cu_1_bsrc), .Ae(cu_1_ae), .Be(cu_1_be), .pc_inc(cu_1_pc_inc), .pc_load(cu_1_pc_load),
    .alu_bus(cu_1_alu_bus), .mem_counter(cu_1_mem_counter), .c_e(cu_1_c_e), .z_e(cu_1_z_e),
    .ram_write(cu_1_ram_write), .ram_read(cu_1_ram_read));
  Multiplexer #(.select(2), .width(8)) multiplexer_1 (
    .in0(b_q), .in1(a_q), .in2(out_2), .in3({8{1'b0}}), .out(multiplexer_1_out), .sel(cu_1_bsrc));
  Counter PC (
    .load(cu_1_pc_load), .D(out_1), .count(cu_1_pc_inc), .Q(PC_q), .up(1'b1), .clk(xnor_1_out), .clr(or_1_out));  // open: carry
  Multiplexer #(.select(2), .width(8)) multiplexer_2 (
    .in0(a_q), .in1(b_q), .in2(out_2), .in3(PC_q), .out(multiplexer_2_out), .sel(cu_1_asrc));
  RAM #(.asyncread("true"), .databus("bidir")) ram_1 (
    .addr(out_4), .we(cu_1_ram_write), .oe(cu_1_ram_read), .clk(not_1_out), .data(out_2));
  Multiplexer #(.select(2), .width(8)) multiplexer_3 (
    .in0(a_q), .in1(b_q), .in2(PC_q), .in3(DBus_past_q), .out(out_4), .sel(cu_1_mem_counter));
  not not_1 (not_1_out, xnor_1_out);
  alu alu_1 (.A(multiplexer_2_out), .B(multiplexer_1_out), .ctrl(cu_1_ctrl), .O(out_1), .Z(alu_1_z), .C(alu_1_c));
  Register #(.width(1)) u_z (.D(alu_1_z), .en(cu_1_c_e), .clk(xnor_1_out), .Q(Z), .clr(or_1_out));
  Register #(.width(1)) u_c (.D(alu_1_c), .en(cu_1_z_e), .clk(xnor_1_out), .Q(C), .clr(or_1_out));
  assign out_2 = cu_1_alu_bus ? out_1 : 8'bz;  // Controlled_Buffer controlled_buffer_1

  assign out_3 = out_2;
endmodule

module cu (
  input  Clk,
  input  R,
  input  [7:0] D_Bus,
  input  Z,
  input  C,
  output [2:0] Ctrl,
  output [1:0] Asrc,
  output [1:0] Bsrc,
  output Ae,
  output Be,
  output pc_inc,
  output pc_load,
  output alu_bus,
  output [1:0] mem_counter,
  output c_e,
  output z_e,
  output ram_write,
  output ram_read
);

  wire AB_out, and_1_out, and_2_out, and_3_out, and_4_out, and_7_out, and_8_out, and_9_out, and_10_out,
       and_11_out, and_12_out, and_13_out, and_14_out, BL_out, controlled_buffer_1_out, d_ff_2_q, d_ff_3_q,
       EQ_out, multiplexer_4_out, nor_1_out, nor_2_out, nor_3_out, nor_4_out, nor_5_out, nor_6_out,
       nor_7_out, nor_8_out, nor_9_out, not_6_out, not_7_out, xor_1_out, xor_3_out, xor_4_out;
  wire [0:0] not_5_out;
  wire [1:0] multiplexer_1_out, multiplexer_2_out, multiplexer_3_out, prev_q_2;
  wire [6:6] and_6_out;
  wire [7:2] prev_q;
  wire [10:7] and_5_out;
  wire [10:10] not_1_out, not_4_out;

  D_Flip_Flop d_ff_1 (.D(1'b0), .clk(Clk), .preset(R));  // open: Q, Qn, reset
  Register prev (.D(D_Bus), .en(1'b1), .clk(Clk), .Q({prev_q, prev_q_2}));  // open: clr
  nor nor_1 (nor_1_out, ~D_Bus[4], D_Bus[5], D_Bus[6], D_Bus[7]);  // NOR_Gate
  nor nor_2 (nor_2_out, D_Bus[4], ~D_Bus[5], D_Bus[6], D_Bus[7]);  // NOR_Gate
  nor nor_3 (nor_3_out, ~D_Bus[4], ~D_Bus[5], D_Bus[6], D_Bus[7]);  // NOR_Gate
  nor nor_4 (nor_4_out, ~D_Bus[4], D_Bus[5], ~D_Bus[6], D_Bus[7]);  // NOR_Gate
  nor nor_5 (nor_5_out, D_Bus[4], D_Bus[5], ~D_Bus[6], D_Bus[7]);  // NOR_Gate
  nor nor_6 (nor_6_out, D_Bus[0], D_Bus[1], D_Bus[2], D_Bus[3], D_Bus[5], D_Bus[6], D_Bus[7], D_Bus[4]);
  and and_1 (and_1_out, nor_6_out, d_ff_2_q);
  assign controlled_buffer_1_out = and_1_out ? and_1_out : 1'bz;  // Controlled_Buffer controlled_buffer_1
  and and_2 (and_2_out, nor_1_out, d_ff_2_q);
  assign controlled_buffer_1_out = and_2_out ? and_2_out : 1'bz;  // Controlled_Buffer controlled_buffer_2
  and and_3 (and_3_out, d_ff_2_q, D_Bus[7]);
  and and_4 (and_4_out, d_ff_2_q, nor_2_out);
  assign controlled_buffer_1_out = and_4_out ? 1'b0 : 1'bz;  // Controlled_Buffer controlled_buffer_3
  D_Flip_Flop d_ff_2 (.D(controlled_buffer_1_out), .clk(Clk), .Q(d_ff_2_q), .preset(R));  // open: Qn, reset
  and and_5 (and_5_out[7], D_Bus[3], D_Bus[2]);
  assign controlled_buffer_1_out = and_3_out ? and_3_out : 1'bz;  // Controlled_Buffer controlled_buffer_4
  Multiplexer #(.select(3), .width(2)) multiplexer_1 (
    .in0(2'b00), .in1(2'b01), .in2(2'b00), .in3(2'b10), .out(multiplexer_1_out), .sel(D_Bus[2:0]));  // open: in4, in5, in6, in7
  not not_1 (not_1_out[10], D_Bus[0]);
  and and_6 (and_6_out[6], d_ff_2_q, nor_3_out);
  assign controlled_buffer_1_out = and_6_out[6] ? 1'b0 : 1'bz;  // Controlled_Buffer controlled_buffer_5
  and and_7 (and_7_out, d_ff_2_q, nor_4_out);
  assign controlled_buffer_1_out = and_7_out ? and_7_out : 1'bz;  // Controlled_Buffer controlled_buffer_6
  and EQ (EQ_out, Z, Z);
  xor xor_1 (xor_1_out, D_Bus[3], EQ_out);
  and and_8 (and_8_out, nor_5_out, d_ff_2_q);
  assign controlled_buffer_1_out = and_8_out ? 1'b0 : 1'bz;  // Controlled_Buffer controlled_buffer_7
  not not_2 (and_5_out[10], D_Bus[2]);
  xor xor_2 (and_5_out[9], D_Bus[2], and_5_out[7]);
  not not_3 (and_5_out[8], and_5_out[7]);
  Multiplexer #(.select(3), .width(2)) multiplexer_2 (
    .in0(2'b00), .in1(2'b01), .in2(2'b10), .in3(2'b00), .out(multiplexer_2_out), .sel(D_Bus[2:0]));  // open: in4, in5, in6, in7
  assign {Ctrl, Asrc, Bsrc, Ae, Be, pc_inc, pc_load, alu_bus, mem_counter, c_e, z_e, ram_write, ram_read} = and_4_out ? {7'b0001011, not_1_out[10], D_Bus[0], 9'h121} : 18'bz;  // Controlled_Buffer controlled_buffer_8
  Multiplexer #(.width(2)) multiplexer_3 (.in0(2'b01), .in1(2'b00), .out(multiplexer_3_out), .sel(D_Bus[0]));
  and AB (AB_out, ~Z, ~C);  // AND_Gate
  xor xor_3 (xor_3_out, D_Bus[3], AB_out);
  not not_4 (not_4_out[10], D_Bus[3]);
  and BL (BL_out, C, C);
  xor xor_4 (xor_4_out, D_Bus[3], BL_out);
  Multiplexer #(.select(2)) multiplexer_4 (
    .in0(1'b1), .in1(xor_1_out), .in2(xor_3_out), .in3(xor_4_out), .out(multiplexer_4_out), .sel(D_Bus[1:0]));
  assign {Ctrl, Asrc, Bsrc, Ae, Be, pc_inc, pc_load, alu_bus, mem_counter, c_e, z_e, ram_write, ram_read} = and_1_out ? 18'h121 : 18'bz;  // Controlled_Buffer controlled_buffer_9
  assign {Ctrl, Asrc, Bsrc, Ae, Be, pc_inc, pc_load, alu_bus, mem_counter, c_e, z_e, ram_write, ram_read} = and_2_out ? {3'b000, D_Bus[1:0], 2'b11, and_5_out, 7'b0100001} : 18'bz;  // Controlled_Buffer controlled_buffer_10
  nor nor_7 (nor_7_out, prev_q[4], ~prev_q[5], prev_q[6], prev_q[7]);  // NOR_Gate
  assign {Ctrl, Asrc, Bsrc, Ae, Be, pc_inc, pc_load, alu_bus, mem_counter, c_e, z_e, ram_write, ram_read} = and_6_out[6] ? {4'b0000, D_Bus[0], 6'b110000, and_6_out[6], multiplexer_3_out, 4'b0010} : 18'bz;  // Controlled_Buffer controlled_buffer_11
  not not_5 (not_5_out[0], D_Bus[0]);
  and and_9 (and_9_out, and_8_out, multiplexer_4_out);
  assign {Ctrl, Asrc, Bsrc, Ae, Be, pc_inc, pc_load, alu_bus, mem_counter, c_e, z_e, ram_write, ram_read} = and_9_out ? 18'h58a1 : 18'bz;  // Controlled_Buffer controlled_buffer_12
  not not_6 (not_6_out, controlled_buffer_1_out);
  assign {Ctrl, Asrc, Bsrc, Ae, Be, pc_inc, pc_load, alu_bus, mem_counter, c_e, z_e, ram_write, ram_read} = and_3_out ? {D_Bus[6:4], multiplexer_1_out, multiplexer_2_out, not_4_out[10], D_Bus[3], 9'h12d} : 18'bz;  // Controlled_Buffer controlled_buffer_13
  and and_10 (and_10_out, d_ff_3_q, nor_7_out);
  assign controlled_buffer_1_out = and_10_out ? and_10_out : 1'bz;  // Controlled_Buffer controlled_buffer_14
  assign {Ctrl, Asrc, Bsrc, Ae, Be, pc_inc, pc_load, alu_bus, mem_counter, c_e, z_e, ram_write, ram_read} = and_7_out ? {4'b0010, D_Bus[1], 1'b0, not_5_out[0], 11'h12d} : 18'bz;  // Controlled_Buffer controlled_buffer_15
  and and_11 (and_11_out, d_ff_2_q, not_6_out);
  and and_12 (and_12_out, d_ff_3_q, nor_8_out);
  nor nor_8 (nor_8_out, ~prev_q[4], ~prev_q[5], prev_q[6], prev_q[7]);  // NOR_Gate
  D_Flip_Flop d_ff_3 (.D(and_11_out), .clk(Clk), .Q(d_ff_3_q), .reset(R));  // open: Qn, preset
  not not_7 (not_7_out, multiplexer_4_out);
  and and_13 (and_13_out, and_8_out, not_7_out);
  assign {Ctrl, Asrc, Bsrc, Ae, Be, pc_inc, pc_load, alu_bus, mem_counter, c_e, z_e, ram_write, ram_read} = and_13_out ? 18'h121 : 18'bz;  // Controlled_Buffer controlled_buffer_16
  nor nor_9 (nor_9_out, prev_q[4], prev_q[5], ~prev_q[6], prev_q[7]);  // NOR_Gate
  assign {Ctrl, Asrc, Bsrc, Ae, Be, pc_inc, pc_load, alu_bus, mem_counter, c_e, z_e, ram_write, ram_read} = and_10_out ? 18'h21 : 18'bz;  // Controlled_Buffer controlled_buffer_17
  assign {Ctrl, Asrc, Bsrc, Ae, Be, pc_inc, pc_load, alu_bus, mem_counter, c_e, z_e, ram_write, ram_read} = and_12_out ? 18'h21 : 18'bz;  // Controlled_Buffer controlled_buffer_18
  assign controlled_buffer_1_out = and_12_out ? and_12_out : 1'bz;  // Controlled_Buffer controlled_buffer_19
  and and_14 (and_14_out, d_ff_3_q, nor_9_out);
  assign {Ctrl, Asrc, Bsrc, Ae, Be, pc_inc, pc_load, alu_bus, mem_counter, c_e, z_e, ram_write, ram_read} = and_14_out ? 18'h121 : 18'bz;  // Controlled_Buffer controlled_buffer_20
  assign controlled_buffer_1_out = and_14_out ? and_14_out : 1'bz;  // Controlled_Buffer controlled_buffer_21

  // Notes on the sheet:
  //   Default State
  //   STORE 0011 r00i
  //   CMP 0101 00rr
  //   NOP 000 0000
  //   MOV r,r 0001 ddss
  //   ALU instructions 1xxx dsss
  //   LOAD 0010 000r
  //   JUMP 0100 n0xx
  //   i - immediate or not
  //    JUMP
  //   Phase 2
  //   DONT JUMP
endmodule

module alu (
  input  [7:0] A,
  input  [7:0] B,
  input  [2:0] ctrl,
  output [7:0] O,
  output Z,
  output C
);

  wire adder_1_cout, shl_1_c, shr_1_c, substractor_1_c;
  wire [7:0] adder_1_out, and_1_out, not_1_out, or_1_out, shl_1_o, shr_1_o, substractor_1_o, xor_1_out;

  // Probe on A
  // Probe on B
  shl shl_1 (.i(A), .o(shl_1_o), .c(shl_1_c));
  shr shr_1 (.i(A), .c(shr_1_c), .o(shr_1_o));
  Adder adder_1 (.a(A), .b(B), .out(adder_1_out), .cout(adder_1_cout));  // open: cin
  substractor substractor_1 (.a(A), .b(B), .c(substractor_1_c), .o(substractor_1_o));
  assign not_1_out = ~A;  // NOT_Gate not_1, 8 bits wide
  assign and_1_out = A & B;  // AND_Gate and_1, 8 bits wide
  assign or_1_out = A | B;  // OR_Gate or_1, 8 bits wide
  assign xor_1_out = A ^ B;  // XOR_Gate xor_1, 8 bits wide
  Multiplexer #(.select(3), .width(8)) multiplexer_1 (
    .in0(adder_1_out), .in1(substractor_1_o), .in2(shl_1_o), .in3(shr_1_o), .in4(not_1_out), .in5(and_1_out),
    .in6(or_1_out), .in7(xor_1_out), .out(O), .sel(ctrl));
  Multiplexer #(.select(2)) multiplexer_2 (
    .in0(adder_1_cout), .in1(substractor_1_c), .in2(shl_1_c), .in3(shr_1_c), .out(C), .sel(ctrl[1:0]));
  // Probe on O
  nor nor_1 (Z, O[0], O[1], O[2], O[3], O[5], O[6], O[7], O[4]);
endmodule

module shr (
  input  [7:0] i,
  output c,
  output [7:0] o
);


  assign c = i[0];
  assign o = {1'b0, i[7:1]};
endmodule

module shl (
  input  [7:0] i,
  output [7:0] o,
  output c
);


  assign c = i[7];
  assign o = {i[6:0], 1'b0};
endmodule

module substractor (
  input  [7:0] a,
  input  [7:0] b,
  output [7:0] o,
  output c
);

  wire or_1_out;
  wire [7:0] multiplexer_1_out, xor_1_out;

  Multiplexer #(.width(8)) multiplexer_1 (.in0({8{1'b0}}), .in1({8{1'b1}}), .out(multiplexer_1_out), .sel(or_1_out));
  assign xor_1_out = b ^ multiplexer_1_out;  // XOR_Gate xor_1, 8 bits wide
  or or_1 (or_1_out, b[0], b[1], b[2], b[3], b[5], b[6], b[7], b[4]);
  Adder adder_1 (.a(a), .b(xor_1_out), .out(o), .cin(or_1_out), .cout(c));
endmodule
